# Fritzing sketch 1-blinkpin11 (saved by Fritzing 0.8.3b)
breadboards: 1

parts:
  Raspberry_Pi_rev1 = Raspberry Pi rev2
  LED1 = LED - 5mm [color="Red (633nm)" package="5 mm [THT]"]
  R1 = Resistor [tolerance=±5% resistance=220 package=THT]

nets:
  N1: Raspberry_Pi_rev1.GND, R1.Pin_0
  N2: Raspberry_Pi_rev1.GPIO_17, LED1.anode
  N3: LED1.cathode, R1.Pin_1
