# Fritzing sketch 2-inputRead (saved by Fritzing 0.8.3b)
breadboards: 1

parts:
  Raspberry_Pi_rev1 = Raspberry Pi rev2
  S1 = Pushbutton [package="[THT]"]
  R2 = Resistor [tolerance=±5% resistance=220 package=THT]

nets:
  N1: Raspberry_Pi_rev1.3V3, S1.Pin_3, S1.Pin_4
  N2: Raspberry_Pi_rev1.GND, R2.Pin_1
  N3: Raspberry_Pi_rev1.GPIO_11, S1.Pin_1, S1.Pin_2, R2.Pin_0
