# Fritzing sketch 2-led+LDR (saved by Fritzing 0.8.3b)
breadboards: 1

parts:
  Raspberry_Pi_rev1 = Raspberry Pi rev2
  LED1 = LED - 5mm [color="Red (633nm)" package="5 mm [THT]"]
  R1 = Resistor [tolerance=±5% resistance=220 package=THT]
  R2 = Resistor [tolerance=±5% resistance=220 package=THT]
  R3 = Photocell (LDR) [package=THT]

nets:
  N1: Raspberry_Pi_rev1.3V3, R3.pin_0
  N2: Raspberry_Pi_rev1.GIPO_2, LED1.cathode
  N3: Raspberry_Pi_rev1.GIPO_3, R2.Pin_0, R3.pin_1
  N4: Raspberry_Pi_rev1.GND, R1.Pin_1, R2.Pin_1
  N5: LED1.anode, R1.Pin_0
