# Fritzing sketch 3-led+switch+ motor (saved by Fritzing 0.8.5b)
breadboards: 1

parts:
  R1 = Resistor [tolerance=±5% resistance=220 package=THT]
  VCC1 = Battery
  LED1 = LED - 5mm [color="Red (633nm)" package="5 mm [THT]"]
  S1 = Pushbutton [package="[THT]"]
  M1 = DC Motor
  S2 = Pushbutton [package="[THT]"]

nets:
  N1: R1.Pin_0, S1.Pin_3, S1.Pin_4
  N2: R1.Pin_1, LED1.anode
  N3: VCC1.-, LED1.cathode, M1.pin_1
  N4: VCC1.+, S1.Pin_1, S1.Pin_2, S2.Pin_1, S2.Pin_2
  N5: M1.pin_2, S2.Pin_3, S2.Pin_4
