# Fritzing sketch 3-potntiometer (saved by Fritzing 0.8.5b)
breadboards: 1

parts:
  VCC1 = Battery
  LED1 = LED - 5mm [color="Red (633nm)" package="5 mm [THT]"]
  R1 = Rotary Potentiometer (Small) [maximum_resistance=100kΩ package=THT]

nets:
  N1: VCC1.-, LED1.cathode
  N2: VCC1.+, R1.leg1, R1.wiper
  N3: LED1.anode, R1.leg2
