# Fritzing sketch 4-PIR (saved by Fritzing 0.8.5b)

parts:
  PIR1 = PIR sensor
  Raspberry_Pi_B_rev1 = Raspberry Pi B rev2

nets:
  VDD: PIR1.VDD, Raspberry_Pi_B_rev1.5V
  N1: PIR1.SIG, Raspberry_Pi_B_rev1.GPIO_11
  GND: PIR1.GND, Raspberry_Pi_B_rev1.GND
