# Fritzing sketch 4.1-PIR with led (saved by Fritzing 0.8.5b)
breadboards: 1

parts:
  PIR1 = PIR sensor
  Raspberry_Pi_B_rev1 = Raspberry Pi B rev2
  R1 = Resistor [tolerance=±5% resistance=220 package=THT]
  LED1 = LED - 5mm [color="Red (633nm)" package="5 mm [THT]"]

nets:
  VDD: PIR1.VDD, Raspberry_Pi_B_rev1.5V
  N1: PIR1.SIG, Raspberry_Pi_B_rev1.GPIO_11
  GND: PIR1.GND, Raspberry_Pi_B_rev1.GND, R1.Pin_0
  N2: Raspberry_Pi_B_rev1.GPIO_17, LED1.anode
  N3: R1.Pin_1, LED1.cathode
