# Fritzing sketch webiopi-TempSensr(DS18B20) (saved by Fritzing 0.8.5b)
breadboards: 1

parts:
  R1 = Resistor [tolerance=±5% resistance=04.7k package=THT]
  Raspberry_Pi_rev1 = Raspberry Pi B rev2
  DS1 = DS18B20 1-Wire Temperature Sensor [part_number=DS18B20]

nets:
  3V3: R1.Pin_0, Raspberry_Pi_rev1.3V3, DS1.VDD
  N1: R1.Pin_1, Raspberry_Pi_rev1.GPIO_4, DS1.DQ
  GND: Raspberry_Pi_rev1.GND, DS1.GND
